// Digital circuit eggtimer.dig as structural Verilog
module eggtimer (
  input  _1_kHz
);

  wire PRESET_out, RST_out, START_out, u_controller_count, u_controller_load, u_controller_start,
       u_counter_endd, u_downcounter_zero;
  wire [3:0] dipswitch_1_out, dipswitch_5_out, dipswitch_9_out, dipswitch_13_out, u_downcounter_m1,
       u_downcounter_m10, u_downcounter_s1, u_downcounter_s10;

  Button #(.activeLow("true")) RST (.out(RST_out));
  Seven_Seg_Hex seven_seg_hex_1 (.d(u_downcounter_m10), .dp(1'b0));
  DipSwitch dipswitch_1 (.out(dipswitch_1_out[3]));
  DipSwitch dipswitch_2 (.out(dipswitch_1_out[2]));
  DipSwitch dipswitch_3 (.out(dipswitch_1_out[1]));
  Seven_Seg_Hex seven_seg_hex_2 (.d(u_downcounter_m1), .dp(1'b1));
  downcounter #(.applicationType("IVERILOG")) u_downcounter (
    .rst(RST_out), .c1khz(_1_kHz), .count(u_controller_count), .load(u_controller_load),
    .pm10(dipswitch_1_out), .pm1(dipswitch_5_out), .ps10(dipswitch_9_out), .ps1(dipswitch_13_out),
    .m10(u_downcounter_m10), .m1(u_downcounter_m1), .s10(u_downcounter_s10), .s1(u_downcounter_s1),
    .zero(u_downcounter_zero));
  DipSwitch dipswitch_4 (.out(dipswitch_1_out[0]));
  DipSwitch dipswitch_5 (.out(dipswitch_5_out[3]));
  DipSwitch dipswitch_6 (.out(dipswitch_5_out[2]));
  Seven_Seg_Hex seven_seg_hex_3 (.d(u_downcounter_s10), .dp(1'b0));
  DipSwitch dipswitch_7 (.out(dipswitch_5_out[1]));
  DipSwitch dipswitch_8 (.out(dipswitch_5_out[0]));
  DipSwitch dipswitch_9 (.out(dipswitch_9_out[3]));
  Seven_Seg_Hex seven_seg_hex_4 (.d(u_downcounter_s1), .dp(1'b0));
  DipSwitch dipswitch_10 (.out(dipswitch_9_out[2]));
  DipSwitch dipswitch_11 (.out(dipswitch_9_out[1]));
  DipSwitch dipswitch_12 (.out(dipswitch_9_out[0]));
  DipSwitch dipswitch_13 (.out(dipswitch_13_out[3]));
  DipSwitch dipswitch_14 (.out(dipswitch_13_out[2]));
  DipSwitch dipswitch_15 (.out(dipswitch_13_out[1]));
  DipSwitch dipswitch_16 (.out(dipswitch_13_out[0]));
  controller #(.applicationType("IVERILOG")) u_controller (
    .c1khz(_1_kHz), .rst(RST_out), .beginn(START_out), .endd(u_counter_endd), .zero(u_downcounter_zero),
    .loadingg(PRESET_out), .load(u_controller_load), .start(u_controller_start), .count(u_controller_count));
  Button START (.out(START_out));
  Button PRESET (.out(PRESET_out));
  counter #(.applicationType("IVERILOG")) u_counter (
    .rst(RST_out), .clk(_1_kHz), .start(u_controller_start), .endd(u_counter_endd));

  // Notes on the sheet:
  //   _1_kHz: Hz: 1000
endmodule

/* Code of downcounter:
module downcounter(
    input rst, c1khz,
    input count, load, 
    input [3:0] pm10,
    input [3:0] pm1,
    input [3:0] ps10,
    input [3:0] ps1,
    output reg [3:0] m10,
    output reg [3:0] m1,
    output reg [3:0] s10,
    output reg [3:0] s1,
    output zero);
    
    reg zero_temp;
    wire [3:0] pm10_temp, pm1_temp, ps10_temp, ps1_temp;

    always @ (posedge c1khz or negedge rst) begin
    
        if(~rst) begin
            m10 <= 0;
            m1 <= 0;
            s10 <= 0;
            s1 <= 0;
	    zero_temp <= 0;
        end
        
        else if(load) begin
            m10 <= pm10_temp;
            m1 <= pm1_temp;
            s10 <= ps10_temp;
            s1 <= ps1_temp;
	    zero_temp <= 0;

	    
        end
        
        else if(count) begin
            
            if(s1 > 0)
                s1 <= s1-1;
            else if(s1 == 0 && s10 > 0) begin
                s10 <= s10-1;
		s1 <= s1 + 9;
	    end
            else if(s1 == 0 && s10 == 0 && m1 > 0) begin
                m1 <= m1-1;
		s10 <= s10 + 5;
		s1 <= s1 + 9;
	    end
            else if(s1 == 0 && s10 == 0 && m1 == 0 && m10 > 0)begin
                m10 <= m10-1;
		m1 <= m1 + 9;
		s10 <= s10 + 5;
		s1 <= s1 + 9;
	    end
            else 
                zero_temp <= 1;
        end
    end

assign zero = zero_temp;
assign ps1_temp = ps1 % 10;
assign ps10_temp = ps10 % 6;
assign pm1_temp = pm1 % 10;
assign pm10_temp = pm10 % 10;
    // insert your counter code here

endmodule
*/

/* Code of controller:
module controller(c1khz, count, load, zero, start, endd, loadingg, beginn, rst);

    input c1khz, rst, beginn, endd, zero, loadingg;
    output reg load, start, count;
    
    parameter idle = 3'd0;
    parameter loading = 3'd1;
    parameter starting = 3'd2;
    parameter timing = 3'd3;
    parameter counting = 3'd4;
    parameter being_zero = 3'd5;
    parameter ending = 3'd6;

    reg [2:0] current_state, next_state;
    
    always @ (posedge c1khz or negedge rst) begin
    	current_state <= next_state;
    end

    always @ (posedge c1khz or negedge rst) begin
	if(~rst)
	    next_state <= idle;
	case(current_state)
	
	     idle: begin
		if(loadingg)
                   next_state <= loading;
                else
                   next_state <= idle;
             end   
             loading: begin
                if(beginn)
                   next_state <= starting;
                else
                   next_state <= loading;
             end
             starting: begin
                 if(zero)
                     next_state <= being_zero;
                 else if(!endd)
                     next_state <= timing;
		 else
		     next_state <= starting;
             end
             timing: begin
		 if(endd)
		     next_state <= counting;
		 else
		     next_state <= timing;
	     end
	     counting: begin
		 next_state <= starting;
	     end
	     being_zero: begin
		 next_state <= ending;
             end
             ending: begin
	         next_state <= idle;
 	     end
	endcase
    end

    always @ (*) begin
	case(current_state)
	
	    idle: begin
		load = 0;
 		count = 0;
		start = 0;
	    end
	    loading: begin
		load = 1;
	    end
	    starting: begin
		start = 1;
		load = 0;
	    end
	    timing: begin
	    start = 0;
		if(endd)
		   count = 1;
		else
		   count = 0;
	    end
	    counting: begin
		 start = 1;
		 count = 0;
	    end
	endcase
   end
		 
endmodule
*/

/* Code of counter:
module counter(
    input rst,
    input clk,
    input start,
    output endd);
    
    reg [9:0] cnt;
    
    assign endd = (cnt==0);
    
    always @(posedge clk, negedge rst)
    begin
        if (~rst)
        begin
            cnt <= 0;
        end
        else
        begin
            if (start)
                cnt <= 999;
            else if (~endd)
                cnt <= cnt-1;
        end
    end // always
endmodule
*/
